// Logisim project calc.circ as structural Verilog: 12 circuits, main circuit main
module main (
);

  wire alu_1_r0, alu_1_r1, alu_1_r2, alu_1_r3, alu_1_r4, alu_1_r5, alu_1_r6, alu_1_r7, hex_7seg_decoder_1_a,
       hex_7seg_decoder_1_b, hex_7seg_decoder_1_c, hex_7seg_decoder_1_d, hex_7seg_decoder_1_e,
       hex_7seg_decoder_1_f, hex_7seg_decoder_1_g, hex_7seg_decoder_2_a, hex_7seg_decoder_2_b,
       hex_7seg_decoder_2_c, hex_7seg_decoder_2_d, hex_7seg_decoder_2_e, hex_7seg_decoder_2_f,
       hex_7seg_decoder_2_g, hex_7seg_decoder_3_a, hex_7seg_decoder_3_b, hex_7seg_decoder_3_c,
       hex_7seg_decoder_3_d, hex_7seg_decoder_3_e, hex_7seg_decoder_3_f, hex_7seg_decoder_3_g,
       hex_7seg_decoder_4_a, hex_7seg_decoder_4_b, hex_7seg_decoder_4_c, hex_7seg_decoder_4_d,
       hex_7seg_decoder_4_e, hex_7seg_decoder_4_f, hex_7seg_decoder_4_g, hex_7seg_decoder_5_a,
       hex_7seg_decoder_5_b, hex_7seg_decoder_5_c, hex_7seg_decoder_5_d, hex_7seg_decoder_5_e,
       hex_7seg_decoder_5_f, hex_7seg_decoder_5_g, hex_7seg_decoder_6_a, hex_7seg_decoder_6_b,
       hex_7seg_decoder_6_c, hex_7seg_decoder_6_d, hex_7seg_decoder_6_e, hex_7seg_decoder_6_f,
       hex_7seg_decoder_6_g, hex_7seg_decoder_7_a, hex_7seg_decoder_7_b, hex_7seg_decoder_7_c,
       hex_7seg_decoder_7_d, hex_7seg_decoder_7_e, hex_7seg_decoder_7_f, hex_7seg_decoder_7_g,
       hex_7seg_decoder_8_a, hex_7seg_decoder_8_b, hex_7seg_decoder_8_c, hex_7seg_decoder_8_d,
       hex_7seg_decoder_8_e, hex_7seg_decoder_8_f, hex_7seg_decoder_8_g, ic_74273_1_y1, ic_74273_1_y2,
       ic_74273_1_y3, ic_74273_1_y4, ic_74273_1_y5, ic_74273_1_y6, ic_74273_1_y7, ic_74273_1_y8, IN_A_sw1,
       IN_A_sw2, IN_A_sw3, IN_A_sw4, IN_A_sw5, IN_A_sw6, IN_A_sw7, IN_A_sw8, IN_B_sw1, IN_B_sw2, IN_B_sw3,
       IN_B_sw4, IN_B_sw5, IN_B_sw6, IN_B_sw7, IN_B_sw8, operation_sw1, operation_sw2, operation_sw3,
       operation_sw4, SAVE_A_out, SAVE_B_out, SAVE_MEM_out, SOURCE_sw1, SOURCE_sw2, user_in_1_reg0,
       user_in_1_reg1, user_in_1_reg2, user_in_1_reg3, user_in_1_reg4, user_in_1_reg5, user_in_1_reg6,
       user_in_1_reg7, user_in_2_reg0, user_in_2_reg1, user_in_2_reg2, user_in_2_reg3, user_in_2_reg4,
       user_in_2_reg5, user_in_2_reg6, user_in_2_reg7;

  DipSwitch #(.number(2)) SOURCE (.sw1(SOURCE_sw1), .sw2(SOURCE_sw2));
  DipSwitch IN_A (
    .sw1(IN_A_sw1), .sw2(IN_A_sw2), .sw3(IN_A_sw3), .sw4(IN_A_sw4), .sw5(IN_A_sw5), .sw6(IN_A_sw6),
    .sw7(IN_A_sw7), .sw8(IN_A_sw8));
  DipSwitch IN_B (
    .sw1(IN_B_sw1), .sw2(IN_B_sw2), .sw3(IN_B_sw3), .sw4(IN_B_sw4), .sw5(IN_B_sw5), .sw6(IN_B_sw6),
    .sw7(IN_B_sw7), .sw8(IN_B_sw8));
  hex_7seg_decoder hex_7seg_decoder_1 (
    .Ai(ic_74273_1_y8), .Bi(ic_74273_1_y7), .Ci(ic_74273_1_y6), .Di(ic_74273_1_y5), .a(hex_7seg_decoder_1_a),
    .e(hex_7seg_decoder_1_e), .b(hex_7seg_decoder_1_b), .c(hex_7seg_decoder_1_c), .d(hex_7seg_decoder_1_d),
    .f(hex_7seg_decoder_1_f), .g(hex_7seg_decoder_1_g));
  hex_7seg_decoder hex_7seg_decoder_2 (
    .Ai(ic_74273_1_y4), .Bi(ic_74273_1_y3), .Ci(ic_74273_1_y2), .Di(ic_74273_1_y1), .a(hex_7seg_decoder_2_a),
    .e(hex_7seg_decoder_2_e), .b(hex_7seg_decoder_2_b), .c(hex_7seg_decoder_2_c), .d(hex_7seg_decoder_2_d),
    .f(hex_7seg_decoder_2_f), .g(hex_7seg_decoder_2_g));
  Button SAVE_A (.out(SAVE_A_out));
  Button SAVE_B (.out(SAVE_B_out));
  _7_Segment_Display u_7_segment_display_1 (
    .g(hex_7seg_decoder_1_g), .f(hex_7seg_decoder_1_f), .a(hex_7seg_decoder_1_a), .b(hex_7seg_decoder_1_b),
    .e(hex_7seg_decoder_1_e), .d(hex_7seg_decoder_1_d), .c(hex_7seg_decoder_1_c));  // open: dp
  _7_Segment_Display u_7_segment_display_2 (
    .g(hex_7seg_decoder_2_g), .f(hex_7seg_decoder_2_f), .a(hex_7seg_decoder_2_a), .b(hex_7seg_decoder_2_b),
    .e(hex_7seg_decoder_2_e), .d(hex_7seg_decoder_2_d), .c(hex_7seg_decoder_2_c));  // open: dp
  user_in user_in_1 (
    .SOURCE(SOURCE_sw1), .SAVE(SAVE_A_out), .MEM0(ic_74273_1_y1), .MEM1(ic_74273_1_y2), .MEM2(ic_74273_1_y3),
    .MEM3(ic_74273_1_y4), .MEM4(ic_74273_1_y5), .MEM5(ic_74273_1_y6), .MEM6(ic_74273_1_y7),
    .MEM7(ic_74273_1_y8), .IN0(IN_A_sw1), .IN1(IN_A_sw2), .IN2(IN_A_sw3), .IN3(IN_A_sw4), .IN4(IN_A_sw5),
    .IN5(IN_A_sw6), .IN6(IN_A_sw7), .IN7(IN_A_sw8), .REG0(user_in_1_reg0), .REG1(user_in_1_reg1),
    .REG2(user_in_1_reg2), .REG3(user_in_1_reg3), .REG4(user_in_1_reg4), .REG5(user_in_1_reg5),
    .REG6(user_in_1_reg6), .REG7(user_in_1_reg7));
  user_in user_in_2 (
    .SOURCE(SOURCE_sw2), .SAVE(SAVE_B_out), .MEM0(ic_74273_1_y1), .MEM1(ic_74273_1_y2), .MEM2(ic_74273_1_y3),
    .MEM3(ic_74273_1_y4), .MEM4(ic_74273_1_y5), .MEM5(ic_74273_1_y6), .MEM6(ic_74273_1_y7),
    .MEM7(ic_74273_1_y8), .IN0(IN_B_sw1), .IN1(IN_B_sw2), .IN2(IN_B_sw3), .IN3(IN_B_sw4), .IN4(IN_B_sw5),
    .IN5(IN_B_sw6), .IN6(IN_B_sw7), .IN7(IN_B_sw8), .REG0(user_in_2_reg0), .REG1(user_in_2_reg1),
    .REG2(user_in_2_reg2), .REG3(user_in_2_reg3), .REG4(user_in_2_reg4), .REG5(user_in_2_reg5),
    .REG6(user_in_2_reg6), .REG7(user_in_2_reg7));
  hex_7seg_decoder hex_7seg_decoder_3 (
    .Ai(user_in_1_reg7), .Bi(user_in_1_reg6), .Ci(user_in_1_reg5), .Di(user_in_1_reg4),
    .a(hex_7seg_decoder_3_a), .e(hex_7seg_decoder_3_e), .b(hex_7seg_decoder_3_b), .c(hex_7seg_decoder_3_c),
    .d(hex_7seg_decoder_3_d), .f(hex_7seg_decoder_3_f), .g(hex_7seg_decoder_3_g));
  hex_7seg_decoder hex_7seg_decoder_4 (
    .Ai(user_in_1_reg3), .Bi(user_in_1_reg2), .Ci(user_in_1_reg1), .Di(user_in_1_reg0),
    .a(hex_7seg_decoder_4_a), .e(hex_7seg_decoder_4_e), .b(hex_7seg_decoder_4_b), .c(hex_7seg_decoder_4_c),
    .d(hex_7seg_decoder_4_d), .f(hex_7seg_decoder_4_f), .g(hex_7seg_decoder_4_g));
  hex_7seg_decoder hex_7seg_decoder_5 (
    .Ai(user_in_2_reg7), .Bi(user_in_2_reg6), .Ci(user_in_2_reg5), .Di(user_in_2_reg4),
    .a(hex_7seg_decoder_5_a), .e(hex_7seg_decoder_5_e), .b(hex_7seg_decoder_5_b), .c(hex_7seg_decoder_5_c),
    .d(hex_7seg_decoder_5_d), .f(hex_7seg_decoder_5_f), .g(hex_7seg_decoder_5_g));
  hex_7seg_decoder hex_7seg_decoder_6 (
    .Ai(user_in_2_reg3), .Bi(user_in_2_reg2), .Ci(user_in_2_reg1), .Di(user_in_2_reg0),
    .a(hex_7seg_decoder_6_a), .e(hex_7seg_decoder_6_e), .b(hex_7seg_decoder_6_b), .c(hex_7seg_decoder_6_c),
    .d(hex_7seg_decoder_6_d), .f(hex_7seg_decoder_6_f), .g(hex_7seg_decoder_6_g));
  _7_Segment_Display u_7_segment_display_3 (
    .g(hex_7seg_decoder_3_g), .f(hex_7seg_decoder_3_f), .a(hex_7seg_decoder_3_a), .b(hex_7seg_decoder_3_b),
    .e(hex_7seg_decoder_3_e), .d(hex_7seg_decoder_3_d), .c(hex_7seg_decoder_3_c));  // open: dp
  _7_Segment_Display u_7_segment_display_4 (
    .g(hex_7seg_decoder_5_g), .f(hex_7seg_decoder_5_f), .a(hex_7seg_decoder_5_a), .b(hex_7seg_decoder_5_b),
    .e(hex_7seg_decoder_5_e), .d(hex_7seg_decoder_5_d), .c(hex_7seg_decoder_5_c));  // open: dp
  _7_Segment_Display u_7_segment_display_5 (
    .g(hex_7seg_decoder_4_g), .f(hex_7seg_decoder_4_f), .a(hex_7seg_decoder_4_a), .b(hex_7seg_decoder_4_b),
    .e(hex_7seg_decoder_4_e), .d(hex_7seg_decoder_4_d), .c(hex_7seg_decoder_4_c));  // open: dp
  _7_Segment_Display u_7_segment_display_6 (
    .g(hex_7seg_decoder_6_g), .f(hex_7seg_decoder_6_f), .a(hex_7seg_decoder_6_a), .b(hex_7seg_decoder_6_b),
    .e(hex_7seg_decoder_6_e), .d(hex_7seg_decoder_6_d), .c(hex_7seg_decoder_6_c));  // open: dp
  DipSwitch #(.number(4)) operation (
    .sw1(operation_sw1), .sw2(operation_sw2), .sw3(operation_sw3), .sw4(operation_sw4));
  ALU alu_1 (
    .ADDsel(operation_sw1), .SUBsel(operation_sw2), .MULsel(operation_sw3), .NANDsel(operation_sw4),
    .A0(user_in_1_reg0), .A1(user_in_1_reg1), .A2(user_in_1_reg2), .A3(user_in_1_reg3), .A4(user_in_1_reg4),
    .A5(user_in_1_reg5), .A6(user_in_1_reg6), .A7(user_in_1_reg7), .B0(user_in_2_reg0), .B1(user_in_2_reg1),
    .B2(user_in_2_reg2), .B3(user_in_2_reg3), .B4(user_in_2_reg4), .B5(user_in_2_reg5), .B6(user_in_2_reg6),
    .B7(user_in_2_reg7), .R0(alu_1_r0), .R1(alu_1_r1), .R2(alu_1_r2), .R3(alu_1_r3), .R4(alu_1_r4),
    .R5(alu_1_r5), .R6(alu_1_r6), .R7(alu_1_r7));
  Button SAVE_MEM (.out(SAVE_MEM_out));
  IC_74273 ic_74273_1 (
    .CLR(1'b1), .CLK(SAVE_MEM_out), .D1(alu_1_r0), .D2(alu_1_r1), .D3(alu_1_r2), .D4(alu_1_r3),
    .D5(alu_1_r4), .D6(alu_1_r5), .D7(alu_1_r6), .D8(alu_1_r7), .Y1(ic_74273_1_y1), .Y2(ic_74273_1_y2),
    .Y3(ic_74273_1_y3), .Y4(ic_74273_1_y4), .Y6(ic_74273_1_y6), .Y7(ic_74273_1_y7), .Y8(ic_74273_1_y8),
    .Y5(ic_74273_1_y5));
  hex_7seg_decoder hex_7seg_decoder_7 (
    .Ai(alu_1_r7), .Bi(alu_1_r6), .Ci(alu_1_r5), .Di(alu_1_r4), .a(hex_7seg_decoder_7_a),
    .e(hex_7seg_decoder_7_e), .b(hex_7seg_decoder_7_b), .c(hex_7seg_decoder_7_c), .d(hex_7seg_decoder_7_d),
    .f(hex_7seg_decoder_7_f), .g(hex_7seg_decoder_7_g));
  _7_Segment_Display u_7_segment_display_7 (
    .g(hex_7seg_decoder_7_g), .f(hex_7seg_decoder_7_f), .a(hex_7seg_decoder_7_a), .b(hex_7seg_decoder_7_b),
    .e(hex_7seg_decoder_7_e), .d(hex_7seg_decoder_7_d), .c(hex_7seg_decoder_7_c));  // open: dp
  hex_7seg_decoder hex_7seg_decoder_8 (
    .Ai(alu_1_r3), .Bi(alu_1_r2), .Ci(alu_1_r1), .Di(alu_1_r0), .a(hex_7seg_decoder_8_a),
    .e(hex_7seg_decoder_8_e), .b(hex_7seg_decoder_8_b), .c(hex_7seg_decoder_8_c), .d(hex_7seg_decoder_8_d),
    .f(hex_7seg_decoder_8_f), .g(hex_7seg_decoder_8_g));
  _7_Segment_Display u_7_segment_display_8 (
    .g(hex_7seg_decoder_8_g), .f(hex_7seg_decoder_8_f), .a(hex_7seg_decoder_8_a), .b(hex_7seg_decoder_8_b),
    .e(hex_7seg_decoder_8_e), .d(hex_7seg_decoder_8_d), .c(hex_7seg_decoder_8_c));  // open: dp
endmodule

module user_in (
  input  SOURCE,
  input  SAVE,
  input  MEM0,
  input  MEM1,
  input  MEM2,
  input  MEM3,
  input  MEM4,
  input  MEM5,
  input  MEM6,
  input  MEM7,
  input  IN0,
  input  IN1,
  input  IN2,
  input  IN3,
  input  IN4,
  input  IN5,
  input  IN6,
  input  IN7,
  output REG0,
  output REG1,
  output REG2,
  output REG3,
  output REG4,
  output REG5,
  output REG6,
  output REG7
);

  IC_74298 ic_74298_1 (
    .S(SOURCE), .CLK(SAVE), .A0(MEM0), .A1(IN0), .B0(MEM1), .B1(IN1), .C0(MEM2), .C1(IN2), .D0(MEM3),
    .D1(IN3), .QA(REG0), .QB(REG1), .QC(REG2), .QD(REG3));
  IC_74298 ic_74298_2 (
    .S(SOURCE), .CLK(SAVE), .A0(MEM4), .A1(IN4), .B0(MEM5), .B1(IN5), .C0(MEM6), .C1(IN6), .D0(MEM7),
    .D1(IN7), .QA(REG4), .QB(REG5), .QC(REG6), .QD(REG7));
endmodule

module IC_74298 (
  input  S,
  input  CLK,
  input  A0,
  input  A1,
  input  B0,
  input  B1,
  input  C0,
  input  C1,
  input  D0,
  input  D1,
  output QA,
  output QB,
  output QC,
  output QD
);

  wire multiplexer_1_out, multiplexer_2_out, multiplexer_3_out, multiplexer_4_out;

  Multiplexer #(.enable("false")) multiplexer_1 (.in0(A0), .in1(A1), .out(multiplexer_1_out), .sel(S));
  Multiplexer #(.enable("false")) multiplexer_2 (.in0(B0), .in1(B1), .out(multiplexer_2_out), .sel(S));
  Multiplexer #(.enable("false")) multiplexer_3 (.in0(C0), .in1(C1), .out(multiplexer_3_out), .sel(S));
  Multiplexer #(.enable("false")) multiplexer_4 (.in0(D0), .in1(D1), .out(multiplexer_4_out), .sel(S));
  D_Flip_Flop #(.trigger("falling")) d_ff_1 (.D(multiplexer_1_out), .clk(CLK), .Q(QA));  // open: Qn, preset, reset
  D_Flip_Flop #(.trigger("falling")) d_ff_2 (.D(multiplexer_2_out), .clk(CLK), .Q(QB));  // open: Qn, preset, reset
  D_Flip_Flop #(.trigger("falling")) d_ff_3 (.D(multiplexer_3_out), .clk(CLK), .Q(QC));  // open: Qn, preset, reset
  D_Flip_Flop #(.trigger("falling")) d_ff_4 (.D(multiplexer_4_out), .clk(CLK), .Q(QD));  // open: Qn, preset, reset
endmodule

module hex_7seg_decoder (
  input  Ai,
  input  Bi,
  input  Ci,
  input  Di,
  output a,
  output e,
  output b,
  output c,
  output d,
  output f,
  output g
);

  wire ic_7408_1_y1, ic_7408_1_y2, ic_7408_1_y3, ic_7408_1_y4, ic_7408_2_y1, ic_7408_2_y2, ic_7408_2_y3,
       ic_7408_2_y4, ic_7408_3_y1, ic_7408_3_y2, ic_7408_3_y3, ic_7408_3_y4, ic_7408_4_y1, ic_7408_4_y2,
       ic_7408_4_y3, ic_7408_4_y4, ic_7408_5_y1, ic_7408_5_y2, ic_7408_5_y3, ic_7408_5_y4, ic_7408_6_y1,
       ic_7408_6_y2, ic_7408_6_y3, ic_7408_6_y4, ic_7408_7_y1, ic_7408_7_y2, ic_7408_7_y3, ic_7408_7_y4,
       ic_7432_1_y1, ic_7432_1_y2, ic_7432_1_y3, ic_7432_1_y4, ic_7432_2_y2, ic_7432_2_y3, ic_7432_3_y1,
       ic_7432_3_y2, ic_7432_3_y3, ic_7432_4_y1, ic_7432_4_y2, ic_7432_4_y3, ic_7432_5_y1, ic_7432_5_y2,
       ic_7432_5_y3, ic_7432_6_y1, ic_7432_6_y2, ic_7432_6_y3, ic_7432_7_y1, ic_7432_7_y2, ic_7432_7_y3,
       not_1_out, not_2_out, not_3_out, not_4_out;

  not not_1 (not_1_out, Ai);
  not not_2 (not_2_out, Bi);
  not not_3 (not_3_out, Ci);
  not not_4 (not_4_out, Di);
  IC_7408 ic_7408_1 (
    .A1(not_2_out), .B1(not_4_out), .A2(not_1_out), .B2(Ci), .A3(Bi), .B3(Ci), .A4(Ai), .B4(not_4_out),
    .Y1(ic_7408_1_y1), .Y2(ic_7408_1_y2), .Y3(ic_7408_1_y3), .Y4(ic_7408_1_y4));
  IC_7408 ic_7408_2 (
    .A1(not_1_out), .B1(Di), .A2(ic_7408_2_y1), .B2(Bi), .A3(Ai), .B3(not_3_out), .A4(ic_7408_2_y3),
    .B4(not_2_out), .Y1(ic_7408_2_y1), .Y2(ic_7408_2_y2), .Y3(ic_7408_2_y3), .Y4(ic_7408_2_y4));
  IC_7408 ic_7408_3 (
    .A1(not_1_out), .B1(not_2_out), .A2(not_1_out), .B2(not_3_out), .A3(ic_7408_3_y2), .B3(not_4_out),
    .A4(ic_7408_2_y3), .B4(Di), .Y1(ic_7408_3_y1), .Y2(ic_7408_3_y2), .Y3(ic_7408_3_y3), .Y4(ic_7408_3_y4));
  IC_7408 ic_7408_4 (
    .A1(ic_7408_1_y2), .B1(Di), .A2(Ci), .B2(not_4_out), .A3(Ai), .B3(Ci), .A4(Ai), .B4(Bi),
    .Y1(ic_7408_4_y1), .Y2(ic_7408_4_y2), .Y3(ic_7408_4_y3), .Y4(ic_7408_4_y4));
  IC_7408 ic_7408_5 (
    .A1(not_3_out), .B1(Di), .A2(not_1_out), .B2(Bi), .A3(Ai), .B3(not_2_out), .A4(ic_7408_1_y1),
    .B4(not_1_out), .Y1(ic_7408_5_y1), .Y2(ic_7408_5_y2), .Y3(ic_7408_5_y3), .Y4(ic_7408_5_y4));
  IC_7408 ic_7408_6 (
    .A1(not_2_out), .B1(Ci), .A2(ic_7408_6_y1), .B2(Di), .A3(ic_7408_5_y1), .B3(Bi), .A4(ic_7408_4_y2),
    .B4(Bi), .Y1(ic_7408_6_y1), .Y2(ic_7408_6_y2), .Y3(ic_7408_6_y3), .Y4(ic_7408_6_y4));
  IC_7408 ic_7408_7 (
    .A1(not_3_out), .B1(not_4_out), .A2(Ai), .B2(Di), .A3(ic_7408_5_y2), .B3(not_3_out), .A4(Bi),
    .B4(not_4_out), .Y1(ic_7408_7_y1), .Y2(ic_7408_7_y2), .Y3(ic_7408_7_y3), .Y4(ic_7408_7_y4));
  IC_7432 ic_7432_1 (
    .A1(ic_7408_1_y1), .B1(ic_7408_2_y2), .A2(ic_7408_1_y2), .B2(ic_7408_2_y4), .A3(ic_7408_1_y3),
    .B3(ic_7432_1_y1), .A4(ic_7408_1_y4), .B4(ic_7432_1_y2), .Y1(ic_7432_1_y1), .Y2(ic_7432_1_y2),
    .Y3(ic_7432_1_y3), .Y4(ic_7432_1_y4));
  IC_7432 ic_7432_2 (
    .A1(ic_7432_1_y3), .B1(ic_7432_1_y4), .A2(ic_7408_1_y1), .B2(ic_7408_4_y2), .A3(ic_7432_2_y2),
    .B3(ic_7408_4_y3), .A4(ic_7432_2_y3), .B4(ic_7408_4_y4), .Y1(a), .Y2(ic_7432_2_y2), .Y3(ic_7432_2_y3),
    .Y4(e));
  IC_7432 ic_7432_3 (
    .A1(ic_7408_3_y1), .B1(ic_7408_1_y1), .A2(ic_7432_3_y1), .B2(ic_7408_3_y3), .A3(ic_7432_3_y2),
    .B3(ic_7408_3_y4), .A4(ic_7432_3_y3), .B4(ic_7408_4_y1), .Y1(ic_7432_3_y1), .Y2(ic_7432_3_y2),
    .Y3(ic_7432_3_y3), .Y4(b));
  IC_7432 ic_7432_4 (
    .A1(ic_7408_3_y2), .B1(ic_7408_2_y1), .A2(ic_7432_4_y1), .B2(ic_7408_5_y1), .A3(ic_7432_4_y2),
    .B3(ic_7408_5_y2), .A4(ic_7432_4_y3), .B4(ic_7408_5_y3), .Y1(ic_7432_4_y1), .Y2(ic_7432_4_y2),
    .Y3(ic_7432_4_y3), .Y4(c));
  IC_7432 ic_7432_5 (
    .A1(ic_7408_2_y3), .B1(ic_7408_5_y4), .A2(ic_7432_5_y1), .B2(ic_7408_6_y2), .A3(ic_7432_5_y2),
    .B3(ic_7408_6_y3), .A4(ic_7432_5_y3), .B4(ic_7408_6_y4), .Y1(ic_7432_5_y1), .Y2(ic_7432_5_y2),
    .Y3(ic_7432_5_y3), .Y4(d));
  IC_7432 ic_7432_6 (
    .A1(ic_7408_7_y1), .B1(ic_7408_7_y4), .A2(ic_7432_6_y1), .B2(ic_7408_5_y3), .A3(ic_7432_6_y2),
    .B3(ic_7408_4_y3), .A4(ic_7432_6_y3), .B4(ic_7408_7_y3), .Y1(ic_7432_6_y1), .Y2(ic_7432_6_y2),
    .Y3(ic_7432_6_y3), .Y4(f));
  IC_7432 ic_7432_7 (
    .A1(ic_7408_4_y2), .B1(ic_7408_6_y1), .A2(ic_7432_7_y1), .B2(ic_7408_5_y3), .A3(ic_7432_7_y2),
    .B3(ic_7408_7_y2), .A4(ic_7432_7_y3), .B4(ic_7408_7_y3), .Y1(ic_7432_7_y1), .Y2(ic_7432_7_y2),
    .Y3(ic_7432_7_y3), .Y4(g));
endmodule

module ALU (
  input  ADDsel,
  input  SUBsel,
  input  MULsel,
  input  NANDsel,
  input  A0,
  input  A1,
  input  A2,
  input  A3,
  input  A4,
  input  A5,
  input  A6,
  input  A7,
  input  B0,
  input  B1,
  input  B2,
  input  B3,
  input  B4,
  input  B5,
  input  B6,
  input  B7,
  output R0,
  output R1,
  output R2,
  output R3,
  output R4,
  output R5,
  output R6,
  output R7
);

  wire adder8_1_s0, adder8_1_s1, adder8_1_s2, adder8_1_s3, adder8_1_s4, adder8_1_s5, adder8_1_s6,
       adder8_1_s7, ic_7400_1_y1, ic_7400_1_y2, ic_7400_1_y3, ic_7400_1_y4, ic_7400_2_y1, ic_7400_2_y2,
       ic_7400_2_y3, ic_7400_2_y4, ic_7400_3_y1, ic_7400_3_y2, ic_7400_3_y3, ic_7400_3_y4, ic_7400_4_y1,
       ic_7400_4_y2, ic_7400_4_y3, ic_7400_4_y4, ic_74148_1_a0, ic_74148_1_a1, ic_74157_1_y1, ic_74157_1_y2,
       ic_74157_1_y3, ic_74157_1_y4, ic_74157_2_y1, ic_74157_2_y2, ic_74157_2_y3, ic_74157_2_y4,
       multiplier8x8_1_prod1, multiplier8x8_1_prod2, multiplier8x8_1_prod3, multiplier8x8_1_prod4,
       multiplier8x8_1_prod5, multiplier8x8_1_prod6, multiplier8x8_1_prod7, multiplier8x8_1_prod8;

  IC_7400 ic_7400_1 (
    .A1(B0), .B1(B0), .A2(B1), .B2(B1), .A3(B2), .B3(B2), .A4(B3), .B4(B3), .Y1(ic_7400_1_y1),
    .Y2(ic_7400_1_y2), .Y3(ic_7400_1_y3), .Y4(ic_7400_1_y4));
  IC_7400 ic_7400_2 (
    .A1(B4), .B1(B4), .A2(B5), .B2(B5), .A3(B6), .B3(B6), .A4(B7), .B4(B7), .Y1(ic_7400_2_y1),
    .Y2(ic_7400_2_y2), .Y3(ic_7400_2_y3), .Y4(ic_7400_2_y4));
  IC_74157 ic_74157_1 (
    .A1(B0), .B1(ic_7400_1_y1), .A2(B1), .B2(ic_7400_1_y2), .A3(B2), .B3(ic_7400_1_y3), .A4(B3),
    .B4(ic_7400_1_y4), .S0(ADDsel), .OE(1'b0), .Y1(ic_74157_1_y1), .Y2(ic_74157_1_y2), .Y3(ic_74157_1_y3),
    .Y4(ic_74157_1_y4));
  IC_74157 ic_74157_2 (
    .A1(B4), .B1(ic_7400_2_y1), .A2(B5), .B2(ic_7400_2_y2), .A3(B6), .B3(ic_7400_2_y3), .A4(B7),
    .B4(ic_7400_2_y4), .S0(ADDsel), .OE(1'b0), .Y1(ic_74157_2_y1), .Y2(ic_74157_2_y2), .Y3(ic_74157_2_y3),
    .Y4(ic_74157_2_y4));
  adder8 adder8_1 (
    .Ci(ADDsel), .A0(A0), .A1(A1), .A2(A2), .A3(A3), .A4(A4), .A5(A5), .A6(A6), .A7(A7), .B0(ic_74157_1_y1),
    .B1(ic_74157_1_y2), .B2(ic_74157_1_y3), .B3(ic_74157_1_y4), .B4(ic_74157_2_y1), .B5(ic_74157_2_y2),
    .B6(ic_74157_2_y3), .B7(ic_74157_2_y4), .S0(adder8_1_s0), .S1(adder8_1_s1), .S2(adder8_1_s2),
    .S3(adder8_1_s3), .S4(adder8_1_s4), .S5(adder8_1_s5), .S6(adder8_1_s6), .S7(adder8_1_s7));  // open: Co
  multiplier8x8 multiplier8x8_1 (
    .MP1(A0), .MP2(A1), .MP3(A2), .MP4(A3), .MP5(A4), .MP6(A5), .MP7(A6), .MP8(A7), .MC1(B0), .MC2(B1),
    .MC3(B2), .MC4(B3), .MC5(B4), .MC6(B5), .MC7(B6), .MC8(B7), .prod1(multiplier8x8_1_prod1),
    .prod2(multiplier8x8_1_prod2), .prod3(multiplier8x8_1_prod3), .prod4(multiplier8x8_1_prod4),
    .prod5(multiplier8x8_1_prod5), .prod6(multiplier8x8_1_prod6), .prod7(multiplier8x8_1_prod7),
    .prod8(multiplier8x8_1_prod8));
  IC_7400 ic_7400_3 (
    .A1(A0), .B1(B0), .A2(A1), .B2(B1), .A3(A2), .B3(B2), .A4(A3), .B4(B3), .Y1(ic_7400_3_y1),
    .Y2(ic_7400_3_y2), .Y3(ic_7400_3_y3), .Y4(ic_7400_3_y4));
  IC_7400 ic_7400_4 (
    .A1(A4), .B1(B4), .A2(A5), .B2(B5), .A3(A6), .B3(B6), .A4(A7), .B4(B7), .Y1(ic_7400_4_y1),
    .Y2(ic_7400_4_y2), .Y3(ic_7400_4_y3), .Y4(ic_7400_4_y4));
  IC_74148 ic_74148_1 (
    .D0(ADDsel), .D1(SUBsel), .D2(MULsel), .D3(NANDsel), .D4(1'b1), .D5(1'b1), .D6(1'b1), .D7(1'b1),
    .EI(1'b0), .A0(ic_74148_1_a0), .A1(ic_74148_1_a1));  // open: EO, GS, A2
  IC_74153 ic_74153_1 (
    .S0(ic_74148_1_a0), .S1(ic_74148_1_a1), .OE1(1'b0), .A1(ic_7400_3_y1), .B1(multiplier8x8_1_prod1),
    .C1(adder8_1_s0), .D1(adder8_1_s0), .OE2(1'b0), .A2(ic_7400_3_y2), .B2(multiplier8x8_1_prod2),
    .C2(adder8_1_s1), .D2(adder8_1_s1), .Y1(R0), .Y2(R1));
  IC_74153 ic_74153_2 (
    .S0(ic_74148_1_a0), .S1(ic_74148_1_a1), .OE1(1'b0), .A1(ic_7400_3_y3), .B1(multiplier8x8_1_prod3),
    .C1(adder8_1_s2), .D1(adder8_1_s2), .OE2(1'b0), .A2(ic_7400_3_y4), .B2(multiplier8x8_1_prod4),
    .C2(adder8_1_s3), .D2(adder8_1_s3), .Y1(R2), .Y2(R3));
  IC_74153 ic_74153_3 (
    .S0(ic_74148_1_a0), .S1(ic_74148_1_a1), .OE1(1'b0), .A1(ic_7400_4_y1), .B1(multiplier8x8_1_prod5),
    .C1(adder8_1_s4), .D1(adder8_1_s4), .OE2(1'b0), .A2(ic_7400_4_y2), .B2(multiplier8x8_1_prod6),
    .C2(adder8_1_s5), .D2(adder8_1_s5), .Y1(R4), .Y2(R5));
  IC_74153 ic_74153_4 (
    .S0(ic_74148_1_a0), .S1(ic_74148_1_a1), .OE1(1'b0), .A1(ic_7400_4_y3), .B1(multiplier8x8_1_prod7),
    .C1(adder8_1_s6), .D1(adder8_1_s6), .OE2(1'b0), .A2(ic_7400_4_y4), .B2(multiplier8x8_1_prod8),
    .C2(adder8_1_s7), .D2(adder8_1_s7), .Y1(R6), .Y2(R7));
endmodule

module adder8 (
  input  Ci,
  input  A0,
  input  A1,
  input  A2,
  input  A3,
  input  A4,
  input  A5,
  input  A6,
  input  A7,
  input  B0,
  input  B1,
  input  B2,
  input  B3,
  input  B4,
  input  B5,
  input  B6,
  input  B7,
  output S0,
  output S1,
  output S2,
  output S3,
  output S4,
  output S5,
  output S6,
  output S7,
  output Co
);

  wire ic_7408_1_y1, ic_7408_1_y2, ic_7408_1_y3, ic_7408_1_y4, ic_7408_2_y1, ic_7408_2_y2, ic_7408_2_y3,
       ic_7408_2_y4, ic_7408_3_y1, ic_7408_3_y2, ic_7408_3_y3, ic_7408_3_y4, ic_7408_4_y1, ic_7408_4_y2,
       ic_7408_4_y3, ic_7408_4_y4, ic_7432_1_y1, ic_7432_1_y2, ic_7432_1_y3, ic_7432_1_y4, ic_7432_2_y1,
       ic_7432_2_y2, ic_7432_2_y3, ic_7486_1_y1, ic_7486_1_y3, ic_7486_2_y1, ic_7486_2_y3, ic_7486_3_y1,
       ic_7486_3_y3, ic_7486_4_y1, ic_7486_4_y3;

  IC_7486 ic_7486_1 (
    .A1(A0), .B1(B0), .A2(ic_7486_1_y1), .B2(Ci), .A3(A1), .B3(B1), .A4(ic_7486_1_y3), .B4(ic_7432_1_y1),
    .Y1(ic_7486_1_y1), .Y2(S0), .Y3(ic_7486_1_y3), .Y4(S1));
  IC_7408 ic_7408_1 (
    .A1(ic_7486_1_y1), .B1(Ci), .A2(A0), .B2(B0), .A3(ic_7486_1_y3), .B3(ic_7432_1_y1), .A4(A1), .B4(B1),
    .Y1(ic_7408_1_y1), .Y2(ic_7408_1_y2), .Y3(ic_7408_1_y3), .Y4(ic_7408_1_y4));
  IC_7486 ic_7486_2 (
    .A1(A2), .B1(B2), .A2(ic_7486_2_y1), .B2(ic_7432_1_y2), .A3(A3), .B3(B3), .A4(ic_7486_2_y3),
    .B4(ic_7432_1_y3), .Y1(ic_7486_2_y1), .Y2(S2), .Y3(ic_7486_2_y3), .Y4(S3));
  IC_7408 ic_7408_2 (
    .A1(ic_7486_2_y1), .B1(ic_7432_1_y2), .A2(A2), .B2(B2), .A3(ic_7486_2_y3), .B3(ic_7432_1_y3), .A4(A3),
    .B4(B3), .Y1(ic_7408_2_y1), .Y2(ic_7408_2_y2), .Y3(ic_7408_2_y3), .Y4(ic_7408_2_y4));
  IC_7486 ic_7486_3 (
    .A1(A4), .B1(B4), .A2(ic_7486_3_y1), .B2(ic_7432_1_y4), .A3(A5), .B3(B5), .A4(ic_7486_3_y3),
    .B4(ic_7432_2_y1), .Y1(ic_7486_3_y1), .Y2(S4), .Y3(ic_7486_3_y3), .Y4(S5));
  IC_7408 ic_7408_3 (
    .A1(ic_7486_3_y1), .B1(ic_7432_1_y4), .A2(A4), .B2(B4), .A3(ic_7486_3_y3), .B3(ic_7432_2_y1), .A4(A5),
    .B4(B5), .Y1(ic_7408_3_y1), .Y2(ic_7408_3_y2), .Y3(ic_7408_3_y3), .Y4(ic_7408_3_y4));
  IC_7486 ic_7486_4 (
    .A1(A6), .B1(B6), .A2(ic_7486_4_y1), .B2(ic_7432_2_y2), .A3(A7), .B3(B7), .A4(ic_7486_4_y3),
    .B4(ic_7432_2_y3), .Y1(ic_7486_4_y1), .Y2(S6), .Y3(ic_7486_4_y3), .Y4(S7));
  IC_7408 ic_7408_4 (
    .A1(ic_7486_4_y1), .B1(ic_7432_2_y2), .A2(A6), .B2(B6), .A3(ic_7486_4_y3), .B3(ic_7432_2_y3), .A4(A7),
    .B4(B7), .Y1(ic_7408_4_y1), .Y2(ic_7408_4_y2), .Y3(ic_7408_4_y3), .Y4(ic_7408_4_y4));
  IC_7432 ic_7432_1 (
    .A1(ic_7408_1_y1), .B1(ic_7408_1_y2), .A2(ic_7408_1_y3), .B2(ic_7408_1_y4), .A3(ic_7408_2_y1),
    .B3(ic_7408_2_y2), .A4(ic_7408_2_y3), .B4(ic_7408_2_y4), .Y1(ic_7432_1_y1), .Y2(ic_7432_1_y2),
    .Y3(ic_7432_1_y3), .Y4(ic_7432_1_y4));
  IC_7432 ic_7432_2 (
    .A1(ic_7408_3_y1), .B1(ic_7408_3_y2), .A2(ic_7408_3_y3), .B2(ic_7408_3_y4), .A3(ic_7408_4_y1),
    .B3(ic_7408_4_y2), .A4(ic_7408_4_y3), .B4(ic_7408_4_y4), .Y1(ic_7432_2_y1), .Y2(ic_7432_2_y2),
    .Y3(ic_7432_2_y3), .Y4(Co));
endmodule

module IC_74251 (
  input  ENABLE,
  input  D0,
  input  D1,
  input  D2,
  input  D3,
  input  D4,
  input  D5,
  input  D6,
  input  D7,
  input  A,
  input  B,
  input  C,
  output Y,
  output W
);

  wire and_1_out, and_2_out, and_3_out, and_4_out, and_5_out, and_6_out, and_7_out, and_8_out, not_1_out,
       not_2_out, not_3_out, not_4_out, not_5_out, not_6_out, not_7_out;

  not not_1 (not_1_out, A);
  not not_2 (not_2_out, B);
  not not_3 (not_3_out, C);
  not not_4 (not_4_out, ENABLE);
  not not_5 (not_5_out, not_1_out);
  not not_6 (not_6_out, not_2_out);
  not not_7 (not_7_out, not_3_out);
  and and_1 (and_1_out, D0, not_1_out, not_2_out, not_3_out, not_4_out);
  and and_2 (and_2_out, D1, not_5_out, not_2_out, not_3_out, not_4_out);
  and and_3 (and_3_out, D2, not_1_out, not_6_out, not_3_out, not_4_out);
  and and_4 (and_4_out, D3, not_5_out, not_6_out, not_3_out, not_4_out);
  and and_5 (and_5_out, D4, not_1_out, not_2_out, not_7_out, not_4_out);
  and and_6 (and_6_out, D5, not_5_out, not_2_out, not_7_out, not_4_out);
  and and_7 (and_7_out, D6, not_1_out, not_6_out, not_7_out, not_4_out);
  and and_8 (and_8_out, D7, not_5_out, not_6_out, not_7_out, not_4_out);
  nor nor_1 (W, and_1_out, and_2_out, and_3_out, and_4_out, and_5_out, and_6_out, and_7_out, and_8_out);
  assign Y = not_4_out ? ~W : 1'bz;  // Controlled_Inverter controlled_inverter_1
endmodule

module multiplier8x8 (
  input  MP1,
  input  MP2,
  input  MP3,
  input  MP4,
  input  MP5,
  input  MP6,
  input  MP7,
  input  MP8,
  input  MC1,
  input  MC2,
  input  MC3,
  input  MC4,
  input  MC5,
  input  MC6,
  input  MC7,
  input  MC8,
  output prod1,
  output prod2,
  output prod3,
  output prod4,
  output prod5,
  output prod6,
  output prod7,
  output prod8
);

  wire adder8_1_s0, adder8_1_s1, adder8_1_s2, adder8_1_s3, adder8_1_s4, adder8_1_s5, adder8_1_s6,
       adder8_1_s7, adder8_2_s0, adder8_2_s1, adder8_2_s2, adder8_2_s3, adder8_2_s4, adder8_2_s5,
       adder8_2_s6, adder8_2_s7, adder8_3_s0, adder8_3_s1, adder8_3_s2, adder8_3_s3, adder8_3_s4,
       adder8_3_s5, adder8_3_s6, adder8_3_s7, adder8_4_s0, adder8_4_s1, adder8_4_s2, adder8_4_s3,
       adder8_4_s4, adder8_4_s5, adder8_4_s6, adder8_4_s7, adder8_5_s0, adder8_5_s1, adder8_5_s2,
       adder8_5_s3, adder8_5_s4, adder8_5_s5, adder8_5_s6, adder8_5_s7, adder8_6_s0, adder8_6_s1,
       adder8_6_s2, adder8_6_s3, adder8_6_s4, adder8_6_s5, adder8_6_s6, adder8_6_s7, multipler1x8_1_prod0,
       multipler1x8_1_prod1, multipler1x8_1_prod2, multipler1x8_1_prod3, multipler1x8_1_prod4,
       multipler1x8_1_prod5, multipler1x8_1_prod6, multipler1x8_1_prod7, multipler1x8_2_prod0,
       multipler1x8_2_prod1, multipler1x8_2_prod2, multipler1x8_2_prod3, multipler1x8_2_prod4,
       multipler1x8_2_prod5, multipler1x8_2_prod6, multipler1x8_2_prod7, multipler1x8_3_prod0,
       multipler1x8_3_prod1, multipler1x8_3_prod2, multipler1x8_3_prod3, multipler1x8_3_prod4,
       multipler1x8_3_prod5, multipler1x8_3_prod6, multipler1x8_3_prod7, multipler1x8_4_prod0,
       multipler1x8_4_prod1, multipler1x8_4_prod2, multipler1x8_4_prod3, multipler1x8_4_prod4,
       multipler1x8_4_prod5, multipler1x8_4_prod6, multipler1x8_4_prod7, multipler1x8_5_prod0,
       multipler1x8_5_prod1, multipler1x8_5_prod2, multipler1x8_5_prod3, multipler1x8_5_prod4,
       multipler1x8_5_prod5, multipler1x8_5_prod6, multipler1x8_5_prod7, multipler1x8_6_prod0,
       multipler1x8_6_prod1, multipler1x8_6_prod2, multipler1x8_6_prod3, multipler1x8_6_prod4,
       multipler1x8_6_prod5, multipler1x8_6_prod6, multipler1x8_6_prod7, multipler1x8_7_prod0,
       multipler1x8_7_prod1, multipler1x8_7_prod2, multipler1x8_7_prod3, multipler1x8_7_prod4,
       multipler1x8_7_prod5, multipler1x8_7_prod6, multipler1x8_7_prod7, multipler1x8_8_prod0,
       multipler1x8_8_prod1, multipler1x8_8_prod2, multipler1x8_8_prod3, multipler1x8_8_prod4,
       multipler1x8_8_prod5, multipler1x8_8_prod6, multipler1x8_8_prod7;

  multipler1X8 multipler1x8_1 (
    .mplier(MP1), .mcand0(MC1), .mcand1(MC2), .mcand2(MC3), .mcand3(MC4), .mcand4(MC5), .mcand5(MC6),
    .mcand6(MC7), .mcand7(MC8), .prod0(multipler1x8_1_prod0), .prod1(multipler1x8_1_prod1),
    .prod2(multipler1x8_1_prod2), .prod3(multipler1x8_1_prod3), .prod4(multipler1x8_1_prod4),
    .prod5(multipler1x8_1_prod5), .prod6(multipler1x8_1_prod6), .prod7(multipler1x8_1_prod7));
  multipler1X8 multipler1x8_2 (
    .mplier(MP2), .mcand0(1'b0), .mcand1(MC1), .mcand2(MC2), .mcand3(MC3), .mcand4(MC4), .mcand5(MC5),
    .mcand6(MC6), .mcand7(MC7), .prod0(multipler1x8_2_prod0), .prod1(multipler1x8_2_prod1),
    .prod2(multipler1x8_2_prod2), .prod3(multipler1x8_2_prod3), .prod4(multipler1x8_2_prod4),
    .prod5(multipler1x8_2_prod5), .prod6(multipler1x8_2_prod6), .prod7(multipler1x8_2_prod7));
  multipler1X8 multipler1x8_3 (
    .mplier(MP3), .mcand0(1'b0), .mcand1(1'b0), .mcand2(MC1), .mcand3(MC2), .mcand4(MC3), .mcand5(MC4),
    .mcand6(MC5), .mcand7(MC6), .prod0(multipler1x8_3_prod0), .prod1(multipler1x8_3_prod1),
    .prod2(multipler1x8_3_prod2), .prod3(multipler1x8_3_prod3), .prod4(multipler1x8_3_prod4),
    .prod5(multipler1x8_3_prod5), .prod6(multipler1x8_3_prod6), .prod7(multipler1x8_3_prod7));
  multipler1X8 multipler1x8_4 (
    .mplier(MP4), .mcand0(1'b0), .mcand1(1'b0), .mcand2(1'b0), .mcand3(MC1), .mcand4(MC2), .mcand5(MC3),
    .mcand6(MC4), .mcand7(MC5), .prod0(multipler1x8_4_prod0), .prod1(multipler1x8_4_prod1),
    .prod2(multipler1x8_4_prod2), .prod3(multipler1x8_4_prod3), .prod4(multipler1x8_4_prod4),
    .prod5(multipler1x8_4_prod5), .prod6(multipler1x8_4_prod6), .prod7(multipler1x8_4_prod7));
  multipler1X8 multipler1x8_5 (
    .mplier(MP5), .mcand0(1'b0), .mcand1(1'b0), .mcand2(1'b0), .mcand3(1'b0), .mcand4(MC1), .mcand5(MC2),
    .mcand6(MC3), .mcand7(MC4), .prod0(multipler1x8_5_prod0), .prod1(multipler1x8_5_prod1),
    .prod2(multipler1x8_5_prod2), .prod3(multipler1x8_5_prod3), .prod4(multipler1x8_5_prod4),
    .prod5(multipler1x8_5_prod5), .prod6(multipler1x8_5_prod6), .prod7(multipler1x8_5_prod7));
  multipler1X8 multipler1x8_6 (
    .mplier(MP6), .mcand0(1'b0), .mcand1(1'b0), .mcand2(1'b0), .mcand3(1'b0), .mcand4(1'b0), .mcand5(MC1),
    .mcand6(MC2), .mcand7(MC3), .prod0(multipler1x8_6_prod0), .prod1(multipler1x8_6_prod1),
    .prod2(multipler1x8_6_prod2), .prod3(multipler1x8_6_prod3), .prod4(multipler1x8_6_prod4),
    .prod5(multipler1x8_6_prod5), .prod6(multipler1x8_6_prod6), .prod7(multipler1x8_6_prod7));
  multipler1X8 multipler1x8_7 (
    .mplier(MP7), .mcand0(1'b0), .mcand1(1'b0), .mcand2(1'b0), .mcand3(1'b0), .mcand4(1'b0), .mcand5(1'b0),
    .mcand6(MC1), .mcand7(MC2), .prod0(multipler1x8_7_prod0), .prod1(multipler1x8_7_prod1),
    .prod2(multipler1x8_7_prod2), .prod3(multipler1x8_7_prod3), .prod4(multipler1x8_7_prod4),
    .prod5(multipler1x8_7_prod5), .prod6(multipler1x8_7_prod6), .prod7(multipler1x8_7_prod7));
  multipler1X8 multipler1x8_8 (
    .mplier(MP8), .mcand0(1'b0), .mcand1(1'b0), .mcand2(1'b0), .mcand3(1'b0), .mcand4(1'b0), .mcand5(1'b0),
    .mcand6(1'b0), .mcand7(MC1), .prod0(multipler1x8_8_prod0), .prod1(multipler1x8_8_prod1),
    .prod2(multipler1x8_8_prod2), .prod3(multipler1x8_8_prod3), .prod4(multipler1x8_8_prod4),
    .prod5(multipler1x8_8_prod5), .prod6(multipler1x8_8_prod6), .prod7(multipler1x8_8_prod7));
  adder8 adder8_1 (
    .Ci(1'b0), .A0(multipler1x8_1_prod0), .A1(multipler1x8_1_prod1), .A2(multipler1x8_1_prod2),
    .A3(multipler1x8_1_prod3), .A4(multipler1x8_1_prod4), .A5(multipler1x8_1_prod5),
    .A6(multipler1x8_1_prod6), .A7(multipler1x8_1_prod7), .B0(multipler1x8_2_prod0),
    .B1(multipler1x8_2_prod1), .B2(multipler1x8_2_prod2), .B3(multipler1x8_2_prod3),
    .B4(multipler1x8_2_prod4), .B5(multipler1x8_2_prod5), .B6(multipler1x8_2_prod6),
    .B7(multipler1x8_2_prod7), .S0(adder8_1_s0), .S1(adder8_1_s1), .S2(adder8_1_s2), .S3(adder8_1_s3),
    .S4(adder8_1_s4), .S5(adder8_1_s5), .S6(adder8_1_s6), .S7(adder8_1_s7));  // open: Co
  adder8 adder8_2 (
    .Ci(1'b0), .A0(adder8_1_s0), .A1(adder8_1_s1), .A2(adder8_1_s2), .A3(adder8_1_s3), .A4(adder8_1_s4),
    .A5(adder8_1_s5), .A6(adder8_1_s6), .A7(adder8_1_s7), .B0(multipler1x8_3_prod0),
    .B1(multipler1x8_3_prod1), .B2(multipler1x8_3_prod2), .B3(multipler1x8_3_prod3),
    .B4(multipler1x8_3_prod4), .B5(multipler1x8_3_prod5), .B6(multipler1x8_3_prod6),
    .B7(multipler1x8_3_prod7), .S0(adder8_2_s0), .S1(adder8_2_s1), .S2(adder8_2_s2), .S3(adder8_2_s3),
    .S4(adder8_2_s4), .S5(adder8_2_s5), .S6(adder8_2_s6), .S7(adder8_2_s7));  // open: Co
  adder8 adder8_3 (
    .Ci(1'b0), .A0(adder8_2_s0), .A1(adder8_2_s1), .A2(adder8_2_s2), .A3(adder8_2_s3), .A4(adder8_2_s4),
    .A5(adder8_2_s5), .A6(adder8_2_s6), .A7(adder8_2_s7), .B0(multipler1x8_4_prod0),
    .B1(multipler1x8_4_prod1), .B2(multipler1x8_4_prod2), .B3(multipler1x8_4_prod3),
    .B4(multipler1x8_4_prod4), .B5(multipler1x8_4_prod5), .B6(multipler1x8_4_prod6),
    .B7(multipler1x8_4_prod7), .S0(adder8_3_s0), .S1(adder8_3_s1), .S2(adder8_3_s2), .S3(adder8_3_s3),
    .S4(adder8_3_s4), .S5(adder8_3_s5), .S6(adder8_3_s6), .S7(adder8_3_s7));  // open: Co
  adder8 adder8_4 (
    .Ci(1'b0), .A0(adder8_3_s0), .A1(adder8_3_s1), .A2(adder8_3_s2), .A3(adder8_3_s3), .A4(adder8_3_s4),
    .A5(adder8_3_s5), .A6(adder8_3_s6), .A7(adder8_3_s7), .B0(multipler1x8_5_prod0),
    .B1(multipler1x8_5_prod1), .B2(multipler1x8_5_prod2), .B3(multipler1x8_5_prod3),
    .B4(multipler1x8_5_prod4), .B5(multipler1x8_5_prod5), .B6(multipler1x8_5_prod6),
    .B7(multipler1x8_5_prod7), .S0(adder8_4_s0), .S1(adder8_4_s1), .S2(adder8_4_s2), .S3(adder8_4_s3),
    .S4(adder8_4_s4), .S5(adder8_4_s5), .S6(adder8_4_s6), .S7(adder8_4_s7));  // open: Co
  adder8 adder8_5 (
    .Ci(1'b0), .A0(adder8_4_s0), .A1(adder8_4_s1), .A2(adder8_4_s2), .A3(adder8_4_s3), .A4(adder8_4_s4),
    .A5(adder8_4_s5), .A6(adder8_4_s6), .A7(adder8_4_s7), .B0(multipler1x8_6_prod0),
    .B1(multipler1x8_6_prod1), .B2(multipler1x8_6_prod2), .B3(multipler1x8_6_prod3),
    .B4(multipler1x8_6_prod4), .B5(multipler1x8_6_prod5), .B6(multipler1x8_6_prod6),
    .B7(multipler1x8_6_prod7), .S0(adder8_5_s0), .S1(adder8_5_s1), .S2(adder8_5_s2), .S3(adder8_5_s3),
    .S4(adder8_5_s4), .S5(adder8_5_s5), .S6(adder8_5_s6), .S7(adder8_5_s7));  // open: Co
  adder8 adder8_6 (
    .Ci(1'b0), .A0(adder8_5_s0), .A1(adder8_5_s1), .A2(adder8_5_s2), .A3(adder8_5_s3), .A4(adder8_5_s4),
    .A5(adder8_5_s5), .A6(adder8_5_s6), .A7(adder8_5_s7), .B0(multipler1x8_7_prod0),
    .B1(multipler1x8_7_prod1), .B2(multipler1x8_7_prod2), .B3(multipler1x8_7_prod3),
    .B4(multipler1x8_7_prod4), .B5(multipler1x8_7_prod5), .B6(multipler1x8_7_prod6),
    .B7(multipler1x8_7_prod7), .S0(adder8_6_s0), .S1(adder8_6_s1), .S2(adder8_6_s2), .S3(adder8_6_s3),
    .S4(adder8_6_s4), .S5(adder8_6_s5), .S6(adder8_6_s6), .S7(adder8_6_s7));  // open: Co
  adder8 adder8_7 (
    .Ci(1'b0), .A0(adder8_6_s0), .A1(adder8_6_s1), .A2(adder8_6_s2), .A3(adder8_6_s3), .A4(adder8_6_s4),
    .A5(adder8_6_s5), .A6(adder8_6_s6), .A7(adder8_6_s7), .B0(multipler1x8_8_prod0),
    .B1(multipler1x8_8_prod1), .B2(multipler1x8_8_prod2), .B3(multipler1x8_8_prod3),
    .B4(multipler1x8_8_prod4), .B5(multipler1x8_8_prod5), .B6(multipler1x8_8_prod6),
    .B7(multipler1x8_8_prod7), .S0(prod1), .S1(prod2), .S2(prod3), .S3(prod4), .S4(prod5), .S5(prod6),
    .S6(prod7), .S7(prod8));  // open: Co
endmodule

module IC_74373 (
  input  D1,
  input  D2,
  input  D3,
  input  D4,
  input  D5,
  input  D6,
  input  D7,
  input  D8,
  input  ENABLE,
  input  OE,
  output Y1,
  output Y2,
  output Y3,
  output Y4,
  output Y5,
  output Y6,
  output Y7,
  output Y8
);

  wire d_latch_1_q, d_latch_2_q, d_latch_3_q, d_latch_4_q, d_latch_5_q, d_latch_6_q, d_latch_7_q,
       d_latch_8_q, not_1_out;

  D_Latch d_latch_1 (.D(D1), .LE(ENABLE), .Q(d_latch_1_q));  // open: R, CLR, SET
  D_Latch d_latch_2 (.D(D2), .LE(ENABLE), .Q(d_latch_2_q));  // open: R, CLR, SET
  D_Latch d_latch_3 (.D(D3), .LE(ENABLE), .Q(d_latch_3_q));  // open: R, CLR, SET
  D_Latch d_latch_4 (.D(D4), .LE(ENABLE), .Q(d_latch_4_q));  // open: R, CLR, SET
  D_Latch d_latch_5 (.D(D5), .LE(ENABLE), .Q(d_latch_5_q));  // open: R, CLR, SET
  D_Latch d_latch_6 (.D(D6), .LE(ENABLE), .Q(d_latch_6_q));  // open: R, CLR, SET
  D_Latch d_latch_7 (.D(D7), .LE(ENABLE), .Q(d_latch_7_q));  // open: R, CLR, SET
  D_Latch d_latch_8 (.D(D8), .LE(ENABLE), .Q(d_latch_8_q));  // open: R, CLR, SET
  not not_1 (not_1_out, OE);
  assign Y1 = not_1_out ? d_latch_1_q : 1'bz;  // Controlled_Buffer controlled_buffer_1
  assign Y2 = not_1_out ? d_latch_2_q : 1'bz;  // Controlled_Buffer controlled_buffer_2
  assign Y3 = not_1_out ? d_latch_3_q : 1'bz;  // Controlled_Buffer controlled_buffer_3
  assign Y4 = not_1_out ? d_latch_4_q : 1'bz;  // Controlled_Buffer controlled_buffer_4
  assign Y5 = not_1_out ? d_latch_5_q : 1'bz;  // Controlled_Buffer controlled_buffer_5
  assign Y6 = not_1_out ? d_latch_6_q : 1'bz;  // Controlled_Buffer controlled_buffer_6
  assign Y7 = not_1_out ? d_latch_7_q : 1'bz;  // Controlled_Buffer controlled_buffer_7
  assign Y8 = not_1_out ? d_latch_8_q : 1'bz;  // Controlled_Buffer controlled_buffer_8
endmodule

module IC_74240 (
  input  OE1,
  input  A1,
  input  A2,
  input  A3,
  input  A4,
  input  OE2,
  input  A5,
  input  A6,
  input  A7,
  input  A8,
  output Y1,
  output Y2,
  output Y3,
  output Y4,
  output Y5,
  output Y6,
  output Y7,
  output Y8
);

  wire not_1_out, not_2_out;

  not not_1 (not_1_out, OE1);
  not not_2 (not_2_out, OE2);
  assign Y1 = not_1_out ? ~A1 : 1'bz;  // Controlled_Inverter controlled_inverter_1
  assign Y2 = not_1_out ? ~A2 : 1'bz;  // Controlled_Inverter controlled_inverter_2
  assign Y3 = not_1_out ? ~A3 : 1'bz;  // Controlled_Inverter controlled_inverter_3
  assign Y4 = not_1_out ? ~A4 : 1'bz;  // Controlled_Inverter controlled_inverter_4
  assign Y5 = not_2_out ? ~A5 : 1'bz;  // Controlled_Inverter controlled_inverter_5
  assign Y6 = not_2_out ? ~A6 : 1'bz;  // Controlled_Inverter controlled_inverter_6
  assign Y7 = not_2_out ? ~A7 : 1'bz;  // Controlled_Inverter controlled_inverter_7
  assign Y8 = not_2_out ? ~A8 : 1'bz;  // Controlled_Inverter controlled_inverter_8
endmodule

module multipler1X8 (
  input  mplier,
  input  mcand0,
  input  mcand1,
  input  mcand2,
  input  mcand3,
  input  mcand4,
  input  mcand5,
  input  mcand6,
  input  mcand7,
  output prod0,
  output prod1,
  output prod2,
  output prod3,
  output prod4,
  output prod5,
  output prod6,
  output prod7
);

  IC_74157 ic_74157_1 (
    .A1(1'b0), .B1(mcand0), .A2(1'b0), .B2(mcand1), .A3(1'b0), .B3(mcand2), .A4(1'b0), .B4(mcand3),
    .S0(mplier), .OE(1'b0), .Y1(prod0), .Y2(prod1), .Y3(prod2), .Y4(prod3));
  IC_74157 ic_74157_2 (
    .A1(1'b0), .B1(mcand4), .A2(1'b0), .B2(mcand5), .A3(1'b0), .B3(mcand6), .A4(1'b0), .B4(mcand7),
    .S0(mplier), .OE(1'b0), .Y1(prod4), .Y2(prod5), .Y3(prod6), .Y4(prod7));
endmodule

module IC_74148 (
  input  D0,
  input  D1,
  input  D2,
  input  D3,
  input  D4,
  input  D5,
  input  D6,
  input  D7,
  input  EI,
  output EO,
  output GS,
  output A0,
  output A1,
  output A2
);

  wire and_1_out, and_2_out, and_3_out, and_4_out, and_5_out, and_6_out, and_7_out, and_8_out, and_9_out,
       and_10_out, and_11_out, and_12_out, not_1_out, not_2_out, not_3_out, not_4_out, not_5_out, not_6_out,
       not_7_out, not_8_out, not_9_out, not_10_out, not_11_out, not_12_out;

  not not_1 (not_1_out, D1);
  not not_2 (not_2_out, D2);
  not not_3 (not_3_out, D3);
  not not_4 (not_4_out, D4);
  not not_5 (not_5_out, D5);
  not not_6 (not_6_out, D6);
  not not_7 (not_7_out, D7);
  not not_8 (not_8_out, EI);
  not not_9 (not_9_out, not_2_out);
  not not_10 (not_10_out, not_4_out);
  not not_11 (not_11_out, not_5_out);
  not not_12 (not_12_out, not_6_out);
  nand nand_1 (EO, D0, D1, D2, D3, D4, D5, D6, D7, not_8_out);
  nand nand_2 (GS, EO, not_8_out);
  and and_1 (and_1_out, not_1_out, not_9_out, not_10_out, not_12_out, not_8_out);
  and and_2 (and_2_out, not_3_out, not_10_out, not_12_out, not_8_out);
  and and_3 (and_3_out, not_5_out, not_12_out, not_8_out);
  and and_4 (and_4_out, not_7_out, not_8_out);
  and and_5 (and_5_out, not_2_out, not_10_out, not_11_out, not_8_out);
  and and_6 (and_6_out, not_3_out, not_10_out, not_11_out, not_8_out);
  and and_7 (and_7_out, not_6_out, not_8_out);
  and and_8 (and_8_out, not_7_out, not_8_out);
  and and_9 (and_9_out, not_4_out, not_8_out);
  and and_10 (and_10_out, not_5_out, not_8_out);
  and and_11 (and_11_out, not_6_out, not_8_out);
  and and_12 (and_12_out, not_7_out, not_8_out);
  nor nor_1 (A0, and_1_out, and_2_out, and_3_out, and_4_out);
  nor nor_2 (A1, and_5_out, and_6_out, and_7_out, and_8_out);
  nor nor_3 (A2, and_9_out, and_10_out, and_11_out, and_12_out);
endmodule
